// Logisim project 1.circ as structural Verilog: 1 circuit, main circuit main
module main (
  input  NOR,
  input  AND,
  input  in_3,
  input  in_4,
  input  in_5,
  input  in_6,
  input  in_7,
  input  in_8,
  input  XOR,
  input  in_10,
  input  in_11,
  input  in_12,
  input  in_13,
  input  AND_2,
  input  in_15,
  input  in_16,
  input  in_17,
  input  in_18,
  input  in_19,
  input  in_20,
  output out_21,
  output out_22,
  output out_23,
  output out_24,
  output out_25,
  output out_26,
  output out_27,
  output out_28,
  output out_29,
  output out_30,
  output out_31
);

  wire nand_1_out, nand_3_out, nand_4_out, nand_5_out, nand_6_out, nand_7_out, nand_11_out, nand_12_out,
       nand_13_out, nand_14_out, nand_15_out, nand_16_out, nand_18_out, nor_1_out, nor_3_out, nor_4_out,
       nor_5_out, nor_6_out, nor_9_out, nor_10_out, nor_11_out, nor_12_out;

  nand nand_1 (nand_1_out, XOR, in_13);
  nand nand_2 (out_30, in_16, in_16);
  nand nand_3 (nand_3_out, AND, in_4);
  nand nand_4 (nand_4_out, in_5, in_5, in_5);
  nand nand_5 (nand_5_out, in_7, in_7);
  nand nand_6 (nand_6_out, XOR, nand_1_out);
  nand nand_7 (nand_7_out, nand_1_out, in_13);
  nand nand_8 (out_22, nand_3_out, nand_3_out);
  nand nand_9 (out_23, nand_4_out, nand_5_out);
  nand nand_10 (out_27, nand_6_out, nand_7_out);
  nand nand_11 (nand_11_out, NOR, NOR);
  nand nand_12 (nand_12_out, in_3, in_3);
  nor nor_1 (nor_1_out, in_19, in_20);
  nand nand_13 (nand_13_out, nand_11_out, nand_12_out);
  nand nand_14 (nand_14_out, in_6, in_8);
  nor nor_2 (out_25, in_10, in_10);
  nor nor_3 (nor_3_out, AND_2, AND_2);
  nor nor_4 (nor_4_out, in_17, in_17);
  nor nor_5 (nor_5_out, in_19, nor_1_out);
  nor nor_6 (nor_6_out, nor_1_out, in_20);
  nand nand_15 (nand_15_out, in_6, nand_14_out);
  nand nand_16 (nand_16_out, nand_14_out, in_8);
  nor nor_7 (out_28, nor_3_out, nor_4_out);
  nand nand_17 (out_21, nand_13_out, nand_13_out);
  nand nand_18 (nand_18_out, nand_15_out, nand_16_out);
  nor nor_8 (out_31, nor_5_out, nor_6_out);
  nor nor_9 (nor_9_out, in_11, in_12);
  nor nor_10 (nor_10_out, in_15, in_15);
  nor nor_11 (nor_11_out, in_18, in_18);
  nand nand_19 (out_24, nand_18_out, nand_18_out);
  nor nor_12 (nor_12_out, nor_10_out, nor_11_out);
  nor nor_13 (out_26, nor_9_out, nor_9_out);
  nor nor_14 (out_29, nor_12_out, nor_12_out);

  // Notes on the sheet:
  //   NOT
  //   OR
  //   XNOR
  //   XNOR
  //   NOT
  //   OR
  //   NAND
endmodule
