// Logisim project 3.circ as structural Verilog: 1 circuit, main circuit main
module main (
  input  in_1,
  input  in_2,
  output out_3,
  output out_4,
  output out_5
);

  wire nand_1_out, nand_2_out, nand_4_out, nand_5_out, nand_6_out, nand_8_out, nand_9_out, nand_10_out,
       nand_12_out, nand_13_out, nand_14_out, nand_15_out, nand_16_out, not_1_out, not_2_out, not_3_out;

  nand nand_1 (nand_1_out, in_1, in_2);
  nand nand_2 (nand_2_out, nand_1_out, in_2);
  not not_1 (not_1_out, in_2);
  nand nand_3 (out_4, nand_1_out, nand_4_out);
  nand nand_4 (nand_4_out, out_4, nand_2_out);
  nand nand_5 (nand_5_out, out_4, nand_4_out);
  nand nand_6 (nand_6_out, nand_5_out, nand_4_out, not_1_out);
  not not_2 (not_2_out, not_1_out);
  nand nand_7 (out_3, nand_5_out, nand_8_out);
  nand nand_8 (nand_8_out, out_3, nand_6_out);
  nand nand_9 (nand_9_out, out_3, nand_8_out);
  nand nand_10 (nand_10_out, nand_9_out, nand_8_out, not_2_out);
  not not_3 (not_3_out, not_2_out);
  nand nand_11 (out_5, nand_9_out, nand_12_out);
  nand nand_12 (nand_12_out, out_5, nand_10_out);
  nand nand_13 (nand_13_out, out_5, nand_12_out);
  nand nand_14 (nand_14_out, nand_13_out, nand_12_out, not_3_out);
  nand nand_15 (nand_15_out, nand_13_out, nand_16_out);
  nand nand_16 (nand_16_out, nand_15_out, nand_14_out);
endmodule
