// Logisim project 4.circ as structural Verilog: 1 circuit, main circuit main
module main (
  input  in_1,
  input  in_2,
  input  in_3,
  input  in_4,
  input  in_5,
  output out_6,
  output out_7,
  output out_8,
  output out_9
);

  wire nand_1_out, nand_2_out, nand_4_out, nand_5_out, nand_6_out, nand_8_out, nand_9_out, nand_10_out,
       nand_12_out, nand_13_out, nand_14_out, nand_16_out, undriven;

  nand nand_1 (nand_1_out, in_1, undriven);
  nand nand_2 (nand_2_out, nand_1_out, in_2);
  nand nand_3 (out_6, nand_1_out, nand_4_out);
  nand nand_4 (nand_4_out, out_6, nand_2_out);
  not nand_5 (nand_5_out, in_3);  // NAND_Gate
  nand nand_6 (nand_6_out, nand_5_out, undriven);
  nand nand_7 (out_7, nand_5_out, nand_8_out);
  nand nand_8 (nand_8_out, out_7, nand_6_out);
  not nand_9 (nand_9_out, in_4);  // NAND_Gate
  nand nand_10 (nand_10_out, nand_9_out, undriven);
  nand nand_11 (out_8, nand_9_out, nand_12_out);
  nand nand_12 (nand_12_out, out_8, nand_10_out);
  not nand_13 (nand_13_out, in_5);  // NAND_Gate
  nand nand_14 (nand_14_out, nand_13_out, undriven);
  nand nand_15 (out_9, nand_13_out, nand_16_out);
  nand nand_16 (nand_16_out, out_9, nand_14_out, undriven);
endmodule
