// Logisim project 6.circ as structural Verilog: 1 circuit, main circuit main
module main (
  input  A,
  input  B,
  input  Cin,
  input  A_2,
  input  B_2,
  input  A_3,
  input  B_3,
  input  A_4,
  input  B_4,
  output out_10,
  output out_11,
  output out_12,
  output out_13,
  output out_14
);

  wire and_1_out, and_2_out, and_3_out, and_4_out, and_5_out, and_6_out, and_7_out, and_8_out, or_1_out,
       or_2_out, or_3_out, xor_1_out, xor_2_out, xor_3_out, xor_4_out;

  xor xor_1 (xor_1_out, A_2, B_2);
  xor xor_2 (xor_2_out, A_3, B_3);
  xor xor_3 (xor_3_out, A, B);
  xor xor_4 (xor_4_out, A_4, B_4);
  xor xor_5 (out_13, xor_3_out, Cin);
  xor xor_6 (out_12, xor_1_out, or_3_out);
  and and_1 (and_1_out, xor_1_out, or_3_out);
  and and_2 (and_2_out, A_2, B_2);
  xor xor_7 (out_11, xor_2_out, or_1_out);
  and and_3 (and_3_out, xor_2_out, or_1_out);
  and and_4 (and_4_out, A_3, B_3);
  xor xor_8 (out_10, xor_4_out, or_2_out);
  and and_5 (and_5_out, xor_3_out, Cin);
  and and_6 (and_6_out, A, B);
  or or_1 (or_1_out, and_1_out, and_2_out);
  or or_2 (or_2_out, and_3_out, and_4_out);
  and and_7 (and_7_out, xor_4_out, or_2_out);
  and and_8 (and_8_out, A_4, B_4);
  or or_3 (or_3_out, and_5_out, and_6_out);
  or or_4 (out_14, and_7_out, and_8_out);

  // Notes on the sheet:
  //   Cin
  //   Cin
  //   Cin
  //   S
  //   S
  //   S
  //   S
  //   Cout
  //   Cout
endmodule
