// Logisim project Encoder.circ as structural Verilog: 1 circuit, main circuit main
module main (
  input  Input,
  input  A3,
  input  A2,
  input  A1,
  input  A0,
  output _0,
  output _1,
  output _2,
  output _3,
  output _4,
  output _5,
  output _6,
  output _7,
  output _8,
  output _9,
  output _10,
  output _11,
  output _12,
  output _13,
  output _14,
  output _15
);

  wire and_1_out, and_2_out, and_3_out, and_4_out, and_5_out, and_6_out, and_7_out, and_8_out, and_9_out,
       and_10_out, and_11_out, and_12_out, and_13_out, and_14_out, and_15_out, and_16_out, and_17_out,
       and_18_out, and_19_out, and_20_out, and_21_out, and_22_out, and_23_out, and_24_out, not_1_out,
       not_2_out, not_3_out, not_4_out;

  not not_1 (not_1_out, A1);
  not not_2 (not_2_out, A0);
  not not_3 (not_3_out, A2);
  and and_1 (and_1_out, not_3_out, not_4_out);
  and and_2 (and_2_out, A1, A0);
  and and_3 (and_3_out, A1, not_2_out);
  and and_4 (and_4_out, not_1_out, A0);
  and and_5 (and_5_out, not_1_out, not_2_out);
  and and_6 (and_6_out, A2, not_4_out);
  and and_7 (and_7_out, and_1_out, and_2_out);
  and and_8 (and_8_out, and_1_out, and_3_out);
  and and_9 (and_9_out, and_1_out, and_4_out);
  and and_10 (and_10_out, and_1_out, and_5_out);
  not not_4 (not_4_out, A3);
  and and_11 (and_11_out, not_3_out, A3);
  and and_12 (and_12_out, and_6_out, and_2_out);
  and and_13 (and_13_out, and_6_out, and_3_out);
  and and_14 (and_14_out, and_6_out, and_4_out);
  and and_15 (and_15_out, and_6_out, and_5_out);
  and and_16 (and_16_out, A2, A3);
  and and_17 (and_17_out, and_11_out, and_2_out);
  and and_18 (and_18_out, and_11_out, and_3_out);
  and and_19 (and_19_out, and_11_out, and_4_out);
  and and_20 (and_20_out, and_11_out, and_5_out);
  and and_21 (and_21_out, and_16_out, and_2_out);
  and and_22 (and_22_out, and_16_out, and_3_out);
  and and_23 (and_23_out, and_16_out, and_4_out);
  and and_24 (and_24_out, and_16_out, and_5_out);
  and and_25 (_0, and_10_out, Input);
  and and_26 (_1, and_9_out, Input);
  and and_27 (_2, and_8_out, Input);
  and and_28 (_3, and_7_out, Input);
  and and_29 (_4, and_15_out, Input);
  and and_30 (_5, and_14_out, Input);
  and and_31 (_6, and_13_out, Input);
  and and_32 (_7, and_12_out, Input);
  and and_33 (_8, and_20_out, Input);
  and and_34 (_9, and_19_out, Input);
  and and_35 (_10, and_18_out, Input);
  and and_36 (_11, and_17_out, Input);
  and and_37 (_12, and_24_out, Input);
  and and_38 (_13, and_23_out, Input);
  and and_39 (_14, and_22_out, Input);
  and and_40 (_15, and_21_out, Input);
endmodule
