// Logisim project osszehasonlito.circ as structural Verilog: 1 circuit, main circuit main
module main (
  input  A3,
  input  A2,
  input  A1,
  input  A0,
  input  B3,
  input  B2,
  input  B1,
  input  B0,
  output A_B,
  output A_B_2,
  output A__B,
  output A_B_3,
  output A__B_2,
  output A_B_4,
  output A_B_5,
  output A__B_3,
  output A_B_6,
  output A_B_7,
  output A__B_4,
  output A_B_8,
  output A_B_9,
  output A__B_5,
  output A_B_10
);

  wire and_5_out, and_6_out, and_7_out, and_8_out, not_1_out, not_2_out, not_3_out, not_4_out;

  not not_1 (not_1_out, A2);
  not not_2 (not_2_out, A3);
  not not_3 (not_3_out, A0);
  not not_4 (not_4_out, A1);
  and and_1 (A_B_4, not_4_out, B1);
  xnor xnor_1 (A__B_3, A1, B1);
  and and_2 (A_B_7, not_1_out, B2);
  xnor xnor_2 (A__B_4, A2, B2);
  and and_3 (A_B_9, not_2_out, B3);
  xnor xnor_3 (A__B_5, A3, B3);
  and and_4 (A_B, not_3_out, B0);
  xnor xnor_4 (A__B, A0, B0);
  nor nor_1 (A_B_3, A__B, A_B);
  nor nor_2 (A_B_6, A__B_3, A_B_4);
  nor nor_3 (A_B_8, A__B_4, A_B_7);
  nor nor_4 (A_B_10, A__B_5, A_B_9);
  buf and_5 (and_5_out, A_B_9);  // AND_Gate
  and and_6 (and_6_out, A__B_5, A__B_4, A_B_4);
  and and_7 (and_7_out, A_B_7, A__B_5);
  and and_8 (and_8_out, A__B_5, A__B_4, A__B_3, A_B);
  or or_1 (A_B_2, and_5_out, and_7_out, and_6_out, and_8_out);
  and and_9 (A__B_2, A__B, A__B_3, A__B_4, A__B_5);
  nor nor_5 (A_B_5, A_B_2, A__B_2);
endmodule
