// Logisim project Összeadó.circ as structural Verilog: 1 circuit, main circuit main
module main (
  input  _1,
  input  _1_2,
  input  _2,
  input  _4,
  input  _8,
  input  _1_3,
  input  _2_2,
  input  _4_2,
  input  _8_2,
  output _1_4,
  output _2_3,
  output _4_3,
  output _8_3,
  output _16
);

  wire and_1_out, and_2_out, and_3_out, and_4_out, and_5_out, and_6_out, and_7_out, and_8_out, or_1_out,
       or_2_out, or_3_out, xor_1_out, xor_2_out, xor_3_out, xor_4_out;

  xor xor_1 (xor_1_out, _1_2, _1_3);
  and and_1 (and_1_out, _1_2, _1_3);
  xor xor_2 (xor_2_out, _2, _2_2);
  and and_2 (and_2_out, _2, _2_2);
  xor xor_3 (xor_3_out, _4, _4_2);
  and and_3 (and_3_out, _4, _4_2);
  xor xor_4 (xor_4_out, _8, _8_2);
  and and_4 (and_4_out, _8, _8_2);
  and and_5 (and_5_out, xor_1_out, _1);
  and and_6 (and_6_out, xor_2_out, or_1_out);
  and and_7 (and_7_out, xor_3_out, or_2_out);
  and and_8 (and_8_out, xor_4_out, or_3_out);
  xor xor_5 (_1_4, xor_1_out, _1);
  or or_1 (or_1_out, and_5_out, and_1_out);
  xor xor_6 (_2_3, xor_2_out, or_1_out);
  or or_2 (or_2_out, and_6_out, and_2_out);
  xor xor_7 (_4_3, xor_3_out, or_2_out);
  or or_3 (or_3_out, and_7_out, and_3_out);
  xor xor_8 (_8_3, xor_4_out, or_3_out);
  or or_4 (_16, and_8_out, and_4_out);

  // Notes on the sheet:
  //   C-in
  //   A
  //   B
  //   O
  //   C-out
endmodule
