// Logisim project 5.circ as structural Verilog: 1 circuit, main circuit main
module main (
  input  in_1,
  output out_2,
  output out_3,
  output out_4,
  output out_5
);

  wire clock_1_out, nand_1_out, nand_2_out, nand_3_out, nand_4_out, nand_5_out, nand_6_out, nand_7_out,
       nand_8_out, nand_9_out, nand_10_out, nand_11_out, nand_12_out, nand_13_out, nand_14_out, nand_15_out,
       nand_16_out, nand_17_out, nand_18_out, nand_19_out, nand_20_out, nand_21_out, nand_22_out,
       nand_23_out, nand_24_out, nand_26_out, nand_28_out, nand_30_out, nand_32_out, not_2_out, not_3_out,
       not_4_out, not_5_out, or_1_out;

  Clock clock_1 (.out(clock_1_out));
  // NOT_Gate not_1 is placed but not wired
  not not_2 (not_2_out, clock_1_out);
  nand nand_1 (nand_1_out, clock_1_out, clock_1_out);
  nand nand_2 (nand_2_out, nand_1_out, nand_1_out, clock_1_out);
  not not_3 (not_3_out, clock_1_out);
  nand nand_3 (nand_3_out, clock_1_out, clock_1_out);
  nand nand_4 (nand_4_out, nand_3_out, nand_3_out, clock_1_out);
  not not_4 (not_4_out, clock_1_out);
  nand nand_5 (nand_5_out, clock_1_out, clock_1_out);
  nand nand_6 (nand_6_out, nand_5_out, nand_5_out, clock_1_out);
  not not_5 (not_5_out, clock_1_out);
  nand nand_7 (nand_7_out, clock_1_out, clock_1_out);
  nand nand_8 (nand_8_out, nand_7_out, nand_7_out, clock_1_out);
  nand nand_9 (nand_9_out, nand_1_out, nand_10_out);
  not nand_10 (nand_10_out, nand_2_out);  // NAND_Gate
  // AND_Gate and_1 is placed but not wired
  nand nand_11 (nand_11_out, nand_3_out, nand_12_out);
  nand nand_12 (nand_12_out, nand_11_out, nand_4_out);
  // AND_Gate and_2 is placed but not wired
  nand nand_13 (nand_13_out, nand_5_out, nand_14_out);
  nand nand_14 (nand_14_out, nand_13_out, nand_6_out);
  // AND_Gate and_3 is placed but not wired
  nand nand_15 (nand_15_out, nand_7_out, nand_16_out);
  nand nand_16 (nand_16_out, nand_15_out, nand_8_out);
  or or_1 (or_1_out, in_1, nand_9_out);
  nand nand_17 (nand_17_out, nand_11_out, not_4_out);
  nand nand_18 (nand_18_out, nand_17_out, nand_17_out, not_4_out);
  nand nand_19 (nand_19_out, nand_13_out, not_5_out);
  nand nand_20 (nand_20_out, nand_19_out, nand_19_out, not_5_out);
  nand nand_21 (nand_21_out, nand_15_out, not_2_out);
  nand nand_22 (nand_22_out, nand_21_out, nand_21_out, not_2_out);
  nand nand_23 (nand_23_out, or_1_out, not_3_out);
  nand nand_24 (nand_24_out, nand_23_out, nand_23_out, not_3_out);
  nand nand_25 (out_3, nand_17_out, nand_26_out);
  nand nand_26 (nand_26_out, out_3, nand_18_out);
  nand nand_27 (out_4, nand_19_out, nand_28_out);
  nand nand_28 (nand_28_out, out_4, nand_20_out);
  nand nand_29 (out_5, nand_21_out, nand_30_out);
  nand nand_30 (nand_30_out, out_5, nand_22_out);
  nand nand_31 (out_2, nand_23_out, nand_32_out);
  nand nand_32 (nand_32_out, out_2, nand_24_out);
endmodule
