// Logisim project 7.circ as structural Verilog: 1 circuit, main circuit main
module main (
  input  \input ,
  input  addr0,
  input  addr1,
  input  addr2,
  input  in_5,
  output out_6,
  output out_7,
  output out_8,
  output out_9,
  output out_10,
  output out_11,
  output out_12,
  output out_13,
  output out_14,
  output out_15,
  output out_16,
  output out_17,
  output out_18,
  output out_19,
  output out_20,
  output out_21
);

  // NOT_Gate not_1 has open pins: in=addr0, out=open
  // NOT_Gate not_2 has open pins: in=addr1, out=open
  // NOT_Gate not_3 has open pins: in=addr2, out=open
  buf and_1 (out_6, \input );  // AND_Gate
  buf and_2 (out_7, \input );  // AND_Gate
  buf and_3 (out_8, \input );  // AND_Gate
  buf and_4 (out_9, \input );  // AND_Gate
  buf and_5 (out_10, \input );  // AND_Gate
  buf and_6 (out_11, \input );  // AND_Gate
  buf and_7 (out_12, \input );  // AND_Gate
  buf and_8 (out_13, \input );  // AND_Gate
  buf and_9 (out_14, \input );  // AND_Gate
  buf and_10 (out_15, \input );  // AND_Gate
  buf and_11 (out_16, \input );  // AND_Gate
  buf and_12 (out_17, \input );  // AND_Gate
  buf and_13 (out_18, \input );  // AND_Gate
  buf and_14 (out_19, \input );  // AND_Gate
  buf and_15 (out_20, \input );  // AND_Gate
  buf and_16 (out_21, \input );  // AND_Gate

  // Notes on the sheet:
  //   addr3
endmodule
