// Logisim project 8.circ as structural Verilog: 1 circuit, main circuit main
module main (
  input  in_1,
  input  in_2,
  input  in_3,
  input  in_4,
  input  in_5,
  input  in_6,
  input  in_7,
  input  in_8,
  input  in_9,
  input  in_10,
  input  in_11,
  input  in_12,
  input  in_13,
  input  in_14,
  input  in_15,
  input  in_16,
  input  in_17,
  input  in_18,
  input  in_19,
  input  in_20,
  input  in_21,
  input  in_22
);

  wire and_1_out, and_2_out, and_3_out, and_4_out, and_5_out, and_6_out, and_15_out, and_16_out, not_1_out,
       not_2_out, not_3_out, not_4_out;

  not not_1 (not_1_out, in_10);
  not not_2 (not_2_out, in_15);
  and and_1 (and_1_out, not_1_out, in_15);
  and and_2 (and_2_out, not_1_out, not_2_out);
  and and_3 (and_3_out, in_10, in_15);
  and and_4 (and_4_out, in_10, not_2_out);
  not not_3 (not_3_out, in_3);
  not not_4 (not_4_out, in_1);
  and and_5 (and_5_out, not_4_out, in_3);
  and and_6 (and_6_out, not_4_out, not_3_out);
  // AND_Gate and_7 has open pins: in0=and_6_out, in1=and_3_out, out=open
  // AND_Gate and_8 has open pins: in0=and_6_out, in1=and_4_out, out=open
  // AND_Gate and_9 has open pins: in0=and_6_out, in1=and_1_out, out=open
  // AND_Gate and_10 has open pins: in0=and_6_out, in1=and_2_out, out=open
  // AND_Gate and_11 has open pins: in0=and_5_out, in1=and_3_out, out=open
  // AND_Gate and_12 has open pins: in0=and_5_out, in1=and_4_out, out=open
  // AND_Gate and_13 has open pins: in0=and_5_out, in1=and_1_out, out=open
  // AND_Gate and_14 has open pins: in0=and_5_out, in1=and_2_out, out=open
  and and_15 (and_15_out, in_1, in_3);
  and and_16 (and_16_out, in_1, not_3_out);
  // AND_Gate and_17 has open pins: in0=and_16_out, in1=and_3_out, out=open
  // AND_Gate and_18 has open pins: in0=and_16_out, in1=and_4_out, out=open
  // AND_Gate and_19 has open pins: in0=and_16_out, in1=and_1_out, out=open
  // AND_Gate and_20 has open pins: in0=and_16_out, in1=and_2_out, out=open
  // AND_Gate and_21 has open pins: in0=and_15_out, in1=and_3_out, out=open
  // AND_Gate and_22 has open pins: in0=and_15_out, in1=and_4_out, out=open
  // AND_Gate and_23 has open pins: in0=and_15_out, in1=and_1_out, out=open
  // AND_Gate and_24 has open pins: in0=and_15_out, in1=and_2_out, out=open
endmodule
