// Logisim project Botlo_Bence_Balazs_134174.circ as structural Verilog: 2 circuits, main circuit adder
module adder (
  input  in_1,
  input  in_2,
  input  in_3,
  input  in_4,
  input  in_5,
  output out_6,
  output out_7,
  output out_8,
  output out_9,
  output out_10
);

  wire and_1_out, and_2_out, and_3_out, and_4_out, and_5_out, and_6_out, and_7_out, and_8_out, or_1_out,
       or_2_out, or_3_out, pull_resistor_1_node, pull_resistor_2_node, xor_1_out, xor_2_out, xor_3_out,
       xor_4_out;

  Pull_Resistor pull_resistor_1 (.node(pull_resistor_1_node));
  Pull_Resistor pull_resistor_2 (.node(pull_resistor_2_node));
  xor xor_1 (xor_1_out, in_1, in_5);
  xor xor_2 (xor_2_out, in_2, pull_resistor_2_node);
  xor xor_3 (xor_3_out, in_3, pull_resistor_2_node);
  xor xor_4 (xor_4_out, in_4, pull_resistor_2_node);
  xor xor_5 (out_6, pull_resistor_1_node, xor_1_out);
  and and_1 (and_1_out, xor_1_out, pull_resistor_1_node);
  and and_2 (and_2_out, in_1, in_5);
  xor xor_6 (out_7, or_1_out, xor_2_out);
  and and_3 (and_3_out, xor_2_out, or_1_out);
  and and_4 (and_4_out, in_2, pull_resistor_2_node);
  xor xor_7 (out_8, or_2_out, xor_3_out);
  and and_5 (and_5_out, xor_3_out, or_2_out);
  and and_6 (and_6_out, in_3, pull_resistor_2_node);
  xor xor_8 (out_9, or_3_out, xor_4_out);
  and and_7 (and_7_out, xor_4_out, or_3_out);
  and and_8 (and_8_out, in_4, pull_resistor_2_node);
  or or_1 (or_1_out, and_1_out, and_2_out);
  or or_2 (or_2_out, and_3_out, and_4_out);
  or or_3 (or_3_out, and_5_out, and_6_out);
  or or_4 (out_10, and_7_out, and_8_out);

  // Notes on the sheet:
  //   Cin
  //   A
  //   B
  //   Cin
  //   A
  //   B
  //   Cin
  //   A
  //   B
  //   Cin
  //   A
  //   B
endmodule

module counter (
  input  in_1,
  input  in_2,
  input  in_3,
  input  in_4,
  input  in_5,
  input  in_6,
  input  in_7,
  input  in_8,
  input  in_9,
  input  in_10,
  input  in_11,
  input  in_12,
  output _8,
  output _4,
  output _2,
  output _1
);

  wire adder_1_out_6, adder_1_out_7, adder_1_out_8, adder_1_out_9, adder_2_out_6, adder_2_out_7,
       adder_2_out_8, adder_2_out_9, adder_3_out_6, adder_3_out_7, adder_3_out_8, adder_3_out_9,
       adder_4_out_6, adder_4_out_7, adder_4_out_8, adder_4_out_9, adder_5_out_6, adder_5_out_7,
       adder_5_out_8, adder_5_out_9, adder_6_out_6, adder_6_out_7, adder_6_out_8, adder_6_out_9,
       adder_7_out_6, adder_7_out_7, adder_7_out_8, adder_7_out_9;

  adder adder_1 (
    .in_1(in_1), .in_2(in_2), .in_3(in_3), .in_4(in_4), .in_5(in_5), .out_6(adder_1_out_6),
    .out_7(adder_1_out_7), .out_8(adder_1_out_8), .out_9(adder_1_out_9));  // open: out_10
  adder adder_2 (
    .in_1(adder_1_out_6), .in_2(adder_1_out_7), .in_3(adder_1_out_8), .in_4(adder_1_out_9), .in_5(in_6),
    .out_6(adder_2_out_6), .out_7(adder_2_out_7), .out_8(adder_2_out_8), .out_9(adder_2_out_9));  // open: out_10
  adder adder_3 (
    .in_1(adder_2_out_6), .in_2(adder_2_out_7), .in_3(adder_2_out_8), .in_4(adder_2_out_9), .in_5(in_7),
    .out_6(adder_3_out_6), .out_7(adder_3_out_7), .out_8(adder_3_out_8), .out_9(adder_3_out_9));  // open: out_10
  adder adder_4 (
    .in_1(adder_3_out_6), .in_2(adder_3_out_7), .in_3(adder_3_out_8), .in_4(adder_3_out_9), .in_5(in_8),
    .out_6(adder_4_out_6), .out_7(adder_4_out_7), .out_8(adder_4_out_8), .out_9(adder_4_out_9));  // open: out_10
  adder adder_5 (
    .in_1(adder_4_out_6), .in_2(adder_4_out_7), .in_3(adder_4_out_8), .in_4(adder_4_out_9), .in_5(in_9),
    .out_6(adder_5_out_6), .out_7(adder_5_out_7), .out_8(adder_5_out_8), .out_9(adder_5_out_9));  // open: out_10
  adder adder_6 (
    .in_1(adder_5_out_6), .in_2(adder_5_out_7), .in_3(adder_5_out_8), .in_4(adder_5_out_9), .in_5(in_10),
    .out_6(adder_6_out_6), .out_7(adder_6_out_7), .out_8(adder_6_out_8), .out_9(adder_6_out_9));  // open: out_10
  adder adder_7 (
    .in_1(adder_6_out_6), .in_2(adder_6_out_7), .in_3(adder_6_out_8), .in_4(adder_6_out_9), .in_5(in_11),
    .out_6(adder_7_out_6), .out_7(adder_7_out_7), .out_8(adder_7_out_8), .out_9(adder_7_out_9));  // open: out_10
  adder adder_8 (
    .in_1(adder_7_out_6), .in_2(adder_7_out_7), .in_3(adder_7_out_8), .in_4(adder_7_out_9), .in_5(in_12),
    .out_6(_1), .out_7(_2), .out_8(_4), .out_9(_8));  // open: out_10
endmodule
