// Logisim project Dekoder.circ as structural Verilog: 1 circuit, main circuit main
module main (
  input  _0,
  input  _1,
  input  _8,
  input  _2,
  input  _4,
  input  _2_2,
  input  _3,
  input  _1_2,
  input  _4_2,
  input  _5,
  input  _6,
  input  _7,
  input  _8_2,
  input  _9,
  input  _10,
  input  _11,
  input  _12,
  input  _13,
  input  _14,
  input  _15,
  output Output
);

  wire and_1_out, and_2_out, and_3_out, and_4_out, and_5_out, and_6_out, and_7_out, and_8_out, and_9_out,
       and_10_out, and_11_out, and_12_out, and_13_out, and_14_out, and_15_out, and_16_out, and_17_out,
       and_18_out, and_19_out, and_20_out, and_21_out, and_22_out, and_23_out, and_24_out, and_25_out,
       and_26_out, and_27_out, and_28_out, and_29_out, and_30_out, and_31_out, and_32_out, and_33_out,
       and_34_out, and_35_out, and_36_out, and_37_out, and_38_out, and_39_out, and_40_out, not_1_out,
       not_2_out, not_3_out, not_4_out, or_1_out, or_2_out, or_3_out, or_4_out, or_5_out, or_6_out, or_7_out,
       or_8_out, or_9_out, or_10_out, or_11_out, or_12_out, or_13_out, or_14_out;

  not not_1 (not_1_out, _2_2);
  not not_2 (not_2_out, _1_2);
  and and_1 (and_1_out, _1_2, not_1_out);
  and and_2 (and_2_out, not_2_out, not_1_out);
  not not_3 (not_3_out, _8);
  not not_4 (not_4_out, _4);
  and and_3 (and_3_out, _1_2, _2_2);
  and and_4 (and_4_out, not_2_out, _2_2);
  and and_5 (and_5_out, _4, not_3_out);
  and and_6 (and_6_out, not_4_out, not_3_out);
  and and_7 (and_7_out, and_3_out, and_6_out);
  and and_8 (and_8_out, and_4_out, and_6_out);
  and and_9 (and_9_out, and_1_out, and_6_out);
  and and_10 (and_10_out, and_2_out, and_6_out);
  and and_11 (and_11_out, _4, _8);
  and and_12 (and_12_out, not_4_out, _8);
  and and_13 (and_13_out, and_3_out, and_5_out);
  and and_14 (and_14_out, and_4_out, and_5_out);
  and and_15 (and_15_out, and_1_out, and_5_out);
  and and_16 (and_16_out, and_2_out, and_5_out);
  and and_17 (and_17_out, and_3_out, and_12_out);
  and and_18 (and_18_out, and_4_out, and_12_out);
  and and_19 (and_19_out, and_1_out, and_12_out);
  and and_20 (and_20_out, and_2_out, and_12_out);
  and and_21 (and_21_out, and_3_out, and_11_out);
  and and_22 (and_22_out, and_4_out, and_11_out);
  and and_23 (and_23_out, and_1_out, and_11_out);
  and and_24 (and_24_out, and_2_out, and_11_out);
  and and_25 (and_25_out, _0, and_10_out);
  and and_26 (and_26_out, _1, and_9_out);
  and and_27 (and_27_out, _2, and_8_out);
  and and_28 (and_28_out, _3, and_7_out);
  and and_29 (and_29_out, _4_2, and_16_out);
  and and_30 (and_30_out, _5, and_15_out);
  and and_31 (and_31_out, _6, and_14_out);
  and and_32 (and_32_out, _7, and_13_out);
  and and_33 (and_33_out, _8_2, and_20_out);
  and and_34 (and_34_out, _9, and_19_out);
  and and_35 (and_35_out, _10, and_18_out);
  and and_36 (and_36_out, _11, and_17_out);
  and and_37 (and_37_out, _12, and_24_out);
  and and_38 (and_38_out, _13, and_23_out);
  and and_39 (and_39_out, _14, and_22_out);
  and and_40 (and_40_out, _15, and_21_out);
  or or_1 (or_1_out, and_25_out, and_26_out);
  or or_2 (or_2_out, and_27_out, and_28_out);
  or or_3 (or_3_out, and_29_out, and_30_out);
  or or_4 (or_4_out, and_31_out, and_32_out);
  or or_5 (or_5_out, and_33_out, and_34_out);
  or or_6 (or_6_out, and_35_out, and_36_out);
  or or_7 (or_7_out, and_37_out, and_38_out);
  or or_8 (or_8_out, and_39_out, and_40_out);
  or or_9 (or_9_out, or_1_out, or_2_out);
  or or_10 (or_10_out, or_3_out, or_4_out);
  or or_11 (or_11_out, or_5_out, or_6_out);
  or or_12 (or_12_out, or_7_out, or_8_out);
  or or_13 (or_13_out, or_9_out, or_10_out);
  or or_14 (or_14_out, or_11_out, or_12_out);
  or or_15 (Output, or_13_out, or_14_out);
endmodule
