// Logisim project Encoder-Dekoder.circ as structural Verilog: 1 circuit, main circuit main
module main (
  input  _8,
  input  _4,
  input  _2,
  input  _1,
  input  Input,
  input  A3,
  input  A2,
  input  A1,
  input  A0,
  output Output
);

  wire and_1_out, and_2_out, and_3_out, and_4_out, and_5_out, and_6_out, and_7_out, and_8_out, and_9_out,
       and_10_out, and_11_out, and_12_out, and_13_out, and_14_out, and_15_out, and_16_out, and_17_out,
       and_18_out, and_19_out, and_20_out, and_21_out, and_22_out, and_23_out, and_24_out, and_25_out,
       and_26_out, and_27_out, and_28_out, and_29_out, and_30_out, and_31_out, and_32_out, and_33_out,
       and_34_out, and_35_out, and_36_out, and_37_out, and_38_out, and_39_out, and_40_out, and_41_out,
       and_42_out, and_43_out, and_44_out, and_45_out, and_46_out, and_47_out, and_48_out, and_49_out,
       and_50_out, and_51_out, and_52_out, and_53_out, and_54_out, and_55_out, and_56_out, and_57_out,
       and_58_out, and_59_out, and_60_out, and_61_out, and_62_out, and_63_out, and_64_out, and_65_out,
       and_66_out, and_67_out, and_68_out, and_69_out, and_70_out, and_71_out, and_72_out, and_73_out,
       and_74_out, and_75_out, and_76_out, and_77_out, and_78_out, and_79_out, and_80_out, not_1_out,
       not_2_out, not_3_out, not_4_out, not_5_out, not_6_out, not_7_out, not_8_out, or_1_out, or_2_out,
       or_3_out, or_4_out, or_5_out, or_6_out, or_7_out, or_8_out, or_9_out, or_10_out, or_11_out, or_12_out,
       or_13_out, or_14_out;

  not not_1 (not_1_out, _2);
  not not_2 (not_2_out, _1);
  not not_3 (not_3_out, A1);
  not not_4 (not_4_out, A0);
  and and_1 (and_1_out, _1, not_1_out);
  and and_2 (and_2_out, not_2_out, not_1_out);
  and and_3 (and_3_out, A1, A0);
  and and_4 (and_4_out, A1, not_4_out);
  and and_5 (and_5_out, not_3_out, A0);
  and and_6 (and_6_out, not_3_out, not_4_out);
  not not_5 (not_5_out, _8);
  not not_6 (not_6_out, _4);
  and and_7 (and_7_out, _1, _2);
  and and_8 (and_8_out, not_2_out, _2);
  not not_7 (not_7_out, A2);
  and and_9 (and_9_out, not_7_out, not_8_out);
  and and_10 (and_10_out, _4, not_5_out);
  and and_11 (and_11_out, not_6_out, not_5_out);
  and and_12 (and_12_out, and_7_out, and_11_out);
  and and_13 (and_13_out, and_8_out, and_11_out);
  and and_14 (and_14_out, and_1_out, and_11_out);
  and and_15 (and_15_out, and_2_out, and_11_out);
  and and_16 (and_16_out, A2, not_8_out);
  and and_17 (and_17_out, and_9_out, and_3_out);
  and and_18 (and_18_out, and_9_out, and_4_out);
  and and_19 (and_19_out, and_9_out, and_5_out);
  and and_20 (and_20_out, and_9_out, and_6_out);
  and and_21 (and_21_out, _4, _8);
  and and_22 (and_22_out, not_6_out, _8);
  not not_8 (not_8_out, A3);
  and and_23 (and_23_out, not_7_out, A3);
  and and_24 (and_24_out, and_16_out, and_3_out);
  and and_25 (and_25_out, and_16_out, and_4_out);
  and and_26 (and_26_out, and_16_out, and_5_out);
  and and_27 (and_27_out, and_16_out, and_6_out);
  and and_28 (and_28_out, and_7_out, and_10_out);
  and and_29 (and_29_out, and_8_out, and_10_out);
  and and_30 (and_30_out, and_1_out, and_10_out);
  and and_31 (and_31_out, and_2_out, and_10_out);
  and and_32 (and_32_out, A2, A3);
  and and_33 (and_33_out, and_7_out, and_22_out);
  and and_34 (and_34_out, and_8_out, and_22_out);
  and and_35 (and_35_out, and_1_out, and_22_out);
  and and_36 (and_36_out, and_2_out, and_22_out);
  and and_37 (and_37_out, and_23_out, and_3_out);
  and and_38 (and_38_out, and_23_out, and_4_out);
  and and_39 (and_39_out, and_23_out, and_5_out);
  and and_40 (and_40_out, and_23_out, and_6_out);
  and and_41 (and_41_out, and_32_out, and_3_out);
  and and_42 (and_42_out, and_32_out, and_4_out);
  and and_43 (and_43_out, and_32_out, and_5_out);
  and and_44 (and_44_out, and_32_out, and_6_out);
  and and_45 (and_45_out, and_7_out, and_21_out);
  and and_46 (and_46_out, and_8_out, and_21_out);
  and and_47 (and_47_out, and_1_out, and_21_out);
  and and_48 (and_48_out, and_2_out, and_21_out);
  and and_49 (and_49_out, and_20_out, Input);
  and and_50 (and_50_out, and_19_out, Input);
  and and_51 (and_51_out, and_18_out, Input);
  and and_52 (and_52_out, and_17_out, Input);
  and and_53 (and_53_out, and_27_out, Input);
  and and_54 (and_54_out, and_26_out, Input);
  and and_55 (and_55_out, and_25_out, Input);
  and and_56 (and_56_out, and_24_out, Input);
  and and_57 (and_57_out, and_40_out, Input);
  and and_58 (and_58_out, and_39_out, Input);
  and and_59 (and_59_out, and_38_out, Input);
  and and_60 (and_60_out, and_37_out, Input);
  and and_61 (and_61_out, and_44_out, Input);
  and and_62 (and_62_out, and_43_out, Input);
  and and_63 (and_63_out, and_42_out, Input);
  and and_64 (and_64_out, and_41_out, Input);
  and and_65 (and_65_out, and_49_out, and_15_out);
  and and_66 (and_66_out, and_50_out, and_14_out);
  and and_67 (and_67_out, and_51_out, and_13_out);
  and and_68 (and_68_out, and_52_out, and_12_out);
  and and_69 (and_69_out, and_53_out, and_31_out);
  and and_70 (and_70_out, and_54_out, and_30_out);
  and and_71 (and_71_out, and_55_out, and_29_out);
  and and_72 (and_72_out, and_56_out, and_28_out);
  and and_73 (and_73_out, and_57_out, and_36_out);
  and and_74 (and_74_out, and_58_out, and_35_out);
  and and_75 (and_75_out, and_59_out, and_34_out);
  and and_76 (and_76_out, and_60_out, and_33_out);
  and and_77 (and_77_out, and_61_out, and_48_out);
  and and_78 (and_78_out, and_62_out, and_47_out);
  and and_79 (and_79_out, and_63_out, and_46_out);
  and and_80 (and_80_out, and_64_out, and_45_out);
  or or_1 (or_1_out, and_65_out, and_66_out);
  or or_2 (or_2_out, and_67_out, and_68_out);
  or or_3 (or_3_out, and_69_out, and_70_out);
  or or_4 (or_4_out, and_71_out, and_72_out);
  or or_5 (or_5_out, and_73_out, and_74_out);
  or or_6 (or_6_out, and_75_out, and_76_out);
  or or_7 (or_7_out, and_77_out, and_78_out);
  or or_8 (or_8_out, and_79_out, and_80_out);
  or or_9 (or_9_out, or_1_out, or_2_out);
  or or_10 (or_10_out, or_3_out, or_4_out);
  or or_11 (or_11_out, or_5_out, or_6_out);
  or or_12 (or_12_out, or_7_out, or_8_out);
  or or_13 (or_13_out, or_9_out, or_10_out);
  or or_14 (or_14_out, or_11_out, or_12_out);
  or or_15 (Output, or_13_out, or_14_out);
endmodule
