// Logisim project FPGA-Shift-és-Dekoder-együtt.circ as structural Verilog: 1 circuit, main circuit main
module main (
  input  in_1,
  input  in_2,
  input  _8,
  input  _4,
  input  _2,
  input  _1,
  input  _4_2,
  input  _5,
  input  _6,
  input  _7,
  input  _8_2,
  input  _9,
  input  _10,
  input  _11,
  input  _12,
  input  _13,
  input  _14,
  input  _15,
  output Output
);

  wire and_1_out, and_2_out, and_3_out, and_4_out, and_5_out, and_6_out, and_7_out, and_8_out, and_9_out,
       and_10_out, and_11_out, and_12_out, and_13_out, and_14_out, and_15_out, and_16_out, and_17_out,
       and_18_out, and_19_out, and_20_out, and_21_out, and_22_out, and_23_out, and_24_out, and_25_out,
       and_26_out, and_27_out, and_28_out, and_29_out, and_30_out, and_31_out, and_32_out, and_33_out,
       and_34_out, and_35_out, and_36_out, and_37_out, and_38_out, and_39_out, and_40_out, nand_1_out,
       nand_2_out, nand_3_out, nand_4_out, nand_5_out, nand_6_out, nand_7_out, nand_8_out, nand_9_out,
       nand_10_out, nand_11_out, nand_12_out, nand_13_out, nand_14_out, nand_15_out, nand_16_out,
       nand_17_out, nand_18_out, nand_19_out, nand_20_out, nand_21_out, nand_22_out, nand_23_out,
       nand_24_out, nand_25_out, nand_26_out, nand_27_out, nand_28_out, nand_29_out, nand_30_out,
       nand_31_out, nand_32_out, not_1_out, not_2_out, not_3_out, not_4_out, not_5_out, not_6_out, not_7_out,
       not_8_out, or_1_out, or_2_out, or_3_out, or_4_out, or_5_out, or_6_out, or_7_out, or_8_out, or_9_out,
       or_10_out, or_11_out, or_12_out, or_13_out, or_15_out;

  nand nand_1 (nand_1_out, in_1, in_2);
  nand nand_2 (nand_2_out, nand_1_out, in_2);
  not not_1 (not_1_out, in_2);
  nand nand_3 (nand_3_out, nand_25_out, in_2);
  nand nand_4 (nand_4_out, nand_3_out, in_2);
  not not_2 (not_2_out, in_2);
  nand nand_5 (nand_5_out, nand_27_out, in_2);
  nand nand_6 (nand_6_out, nand_5_out, in_2);
  not not_3 (not_3_out, in_2);
  nand nand_7 (nand_7_out, nand_29_out, in_2);
  nand nand_8 (nand_8_out, nand_7_out, in_2);
  not not_4 (not_4_out, in_2);
  not not_5 (not_5_out, _2);
  and and_1 (and_1_out, _1, not_5_out);
  not not_6 (not_6_out, _1);
  and and_2 (and_2_out, not_6_out, not_5_out);
  nand nand_9 (nand_9_out, nand_1_out, nand_10_out);
  nand nand_10 (nand_10_out, nand_9_out, nand_2_out);
  nand nand_11 (nand_11_out, nand_3_out, nand_12_out);
  nand nand_12 (nand_12_out, nand_11_out, nand_4_out);
  nand nand_13 (nand_13_out, nand_5_out, nand_14_out);
  nand nand_14 (nand_14_out, nand_13_out, nand_6_out);
  nand nand_15 (nand_15_out, nand_7_out, nand_16_out);
  nand nand_16 (nand_16_out, nand_15_out, nand_8_out);
  not not_7 (not_7_out, _8);
  not not_8 (not_8_out, _4);
  and and_3 (and_3_out, _1, _2);
  and and_4 (and_4_out, not_6_out, _2);
  nand nand_17 (nand_17_out, nand_9_out, not_1_out);
  nand nand_18 (nand_18_out, nand_17_out, not_1_out);
  nand nand_19 (nand_19_out, nand_11_out, not_2_out);
  nand nand_20 (nand_20_out, nand_19_out, not_2_out);
  nand nand_21 (nand_21_out, nand_13_out, not_3_out);
  nand nand_22 (nand_22_out, nand_21_out, not_3_out);
  nand nand_23 (nand_23_out, nand_15_out, not_4_out);
  nand nand_24 (nand_24_out, nand_23_out, not_4_out);
  and and_5 (and_5_out, _4, not_7_out);
  and and_6 (and_6_out, not_8_out, not_7_out);
  and and_7 (and_7_out, and_3_out, and_6_out);
  and and_8 (and_8_out, and_4_out, and_6_out);
  and and_9 (and_9_out, and_1_out, and_6_out);
  and and_10 (and_10_out, and_2_out, and_6_out);
  nand nand_25 (nand_25_out, nand_17_out, nand_26_out);
  nand nand_26 (nand_26_out, nand_25_out, nand_18_out);
  nand nand_27 (nand_27_out, nand_19_out, nand_28_out);
  nand nand_28 (nand_28_out, nand_27_out, nand_20_out);
  nand nand_29 (nand_29_out, nand_21_out, nand_30_out);
  nand nand_30 (nand_30_out, nand_29_out, nand_22_out);
  nand nand_31 (nand_31_out, nand_23_out, nand_32_out);
  nand nand_32 (nand_32_out, nand_31_out, nand_24_out);
  and and_11 (and_11_out, _4, _8);
  and and_12 (and_12_out, not_8_out, _8);
  and and_13 (and_13_out, and_3_out, and_5_out);
  and and_14 (and_14_out, and_4_out, and_5_out);
  and and_15 (and_15_out, and_1_out, and_5_out);
  and and_16 (and_16_out, and_2_out, and_5_out);
  and and_17 (and_17_out, and_3_out, and_12_out);
  and and_18 (and_18_out, and_4_out, and_12_out);
  and and_19 (and_19_out, and_1_out, and_12_out);
  and and_20 (and_20_out, and_2_out, and_12_out);
  and and_21 (and_21_out, and_3_out, and_11_out);
  and and_22 (and_22_out, and_4_out, and_11_out);
  and and_23 (and_23_out, and_1_out, and_11_out);
  and and_24 (and_24_out, and_2_out, and_11_out);
  and and_25 (and_25_out, nand_25_out, and_10_out);
  and and_26 (and_26_out, nand_27_out, and_9_out);
  and and_27 (and_27_out, nand_29_out, and_8_out);
  and and_28 (and_28_out, nand_31_out, and_7_out);
  and and_29 (and_29_out, _4_2, and_16_out);
  and and_30 (and_30_out, _5, and_15_out);
  and and_31 (and_31_out, _6, and_14_out);
  and and_32 (and_32_out, _7, and_13_out);
  and and_33 (and_33_out, _8_2, and_20_out);
  and and_34 (and_34_out, _9, and_19_out);
  and and_35 (and_35_out, _10, and_18_out);
  and and_36 (and_36_out, _11, and_17_out);
  and and_37 (and_37_out, _12, and_24_out);
  and and_38 (and_38_out, _13, and_23_out);
  and and_39 (and_39_out, _14, and_22_out);
  and and_40 (and_40_out, _15, and_21_out);
  or or_1 (or_1_out, and_25_out, and_26_out);
  or or_2 (or_2_out, and_27_out, and_28_out);
  or or_3 (or_3_out, and_29_out, and_30_out);
  or or_4 (or_4_out, and_31_out, and_32_out);
  or or_5 (or_5_out, and_33_out, and_34_out);
  or or_6 (or_6_out, and_35_out, and_36_out);
  or or_7 (or_7_out, and_37_out, and_38_out);
  or or_8 (or_8_out, and_39_out, and_40_out);
  or or_9 (or_9_out, or_1_out, or_2_out);
  or or_10 (or_10_out, or_3_out, or_4_out);
  or or_11 (or_11_out, or_5_out, or_6_out);
  or or_12 (or_12_out, or_7_out, or_8_out);
  or or_13 (or_13_out, or_9_out, or_10_out);
  or or_14 (Output, or_13_out, or_15_out);
  or or_15 (or_15_out, or_11_out, or_12_out);

  // Notes on the sheet:
  //   1
  //   2
  //   3
endmodule
