// Logisim project NAnd-kapuk.circ as structural Verilog: 1 circuit, main circuit main
module main (
  input  in_1,
  input  in_2,
  input  in_3,
  input  in_4,
  input  in_5,
  input  in_6,
  input  in_7,
  input  in_8,
  input  in_9,
  input  in_10,
  input  in_11,
  input  in_12,
  input  in_13,
  input  in_14,
  input  in_15,
  input  in_16,
  input  in_17,
  input  in_18,
  input  in_19,
  input  in_20,
  input  in_21,
  output out_22,
  output out_23,
  output out_24,
  output out_25,
  output out_26,
  output NXor___XNor,
  output out_28,
  output out_29,
  output out_30,
  output out_31,
  output out_32,
  output out_33
);

  wire nand_2_out, nand_3_out, nand_4_out, nand_5_out, nand_7_out, nand_8_out, nand_10_out, nand_11_out,
       nand_16_out, nand_17_out, nand_18_out, nand_19_out, nand_20_out, nand_21_out, nand_23_out,
       nand_24_out, nand_29_out, nand_30_out, nand_31_out, nand_32_out;

  nand nand_1 (out_26, in_9, in_9);
  nand nand_2 (nand_2_out, in_12, in_12);
  nand nand_3 (nand_3_out, in_14, in_16);
  not nand_4 (nand_4_out, in_17);  // NAND_Gate
  nand nand_5 (nand_5_out, in_2, in_2, in_4, in_4);
  nand nand_6 (out_24, in_5, in_5, in_7);
  not nand_7 (nand_7_out, in_18);  // NAND_Gate
  not nand_8 (nand_8_out, in_20);  // NAND_Gate
  not nand_9 (out_28, nand_2_out);  // NAND_Gate
  not nand_10 (nand_10_out, nand_3_out);  // NAND_Gate
  not nand_11 (nand_11_out, nand_4_out);  // NAND_Gate
  nand nand_12 (out_32, nand_7_out, nand_7_out, nand_8_out);
  nand nand_13 (out_23, nand_5_out, nand_5_out);
  not nand_14 (out_30, nand_10_out);  // NAND_Gate
  not nand_15 (out_31, nand_11_out);  // NAND_Gate
  nand nand_16 (nand_16_out, in_1, in_1, in_3, in_3);
  nand nand_17 (nand_17_out, in_13, in_15);
  not nand_18 (nand_18_out, in_19);  // NAND_Gate
  not nand_19 (nand_19_out, in_21);  // NAND_Gate
  nand nand_20 (nand_20_out, in_6, in_6, in_8, in_8);
  nand nand_21 (nand_21_out, in_13, nand_17_out);
  nand nand_22 (out_29, nand_21_out, nand_21_out, nand_23_out);
  nand nand_23 (nand_23_out, nand_17_out, in_15);
  nand nand_24 (nand_24_out, nand_18_out, nand_18_out, nand_19_out);
  not nand_25 (out_22, nand_16_out);  // NAND_Gate
  not nand_26 (out_22, nand_16_out);  // NAND_Gate
  not nand_27 (out_33, nand_24_out);  // NAND_Gate
  not nand_28 (out_25, nand_20_out);  // NAND_Gate
  nand nand_29 (nand_29_out, in_10, in_11);
  nand nand_30 (nand_30_out, nand_29_out, in_11);
  nand nand_31 (nand_31_out, in_10, nand_29_out);
  nand nand_32 (nand_32_out, nand_31_out, nand_31_out, nand_30_out);
  not nand_33 (NXor___XNor, nand_32_out);  // NAND_Gate

  // Notes on the sheet:
  //   And
  //   NAnd
  //   Not
  //   Or
  //   Xor
  //   Nor
endmodule
