// Logisim project dhgssdf.circ as structural Verilog: 1 circuit, main circuit main
module main (
  input  in_1,
  input  in_2,
  input  in_3,
  input  in_4,
  input  in_5,
  input  in_6,
  input  in_7,
  input  in_8,
  input  in_9,
  input  in_10,
  input  in_11,
  input  in_12,
  output out_13,
  output out_14,
  output out_15,
  output out_16,
  output out_17,
  output out_18,
  output out_19,
  output out_20
);

  wire d_ff_1_q, d_ff_2_q, d_ff_3_q, d_ff_4_q, nand_1_out, nand_2_out, nand_3_out, nand_4_out, nand_5_out,
       nand_6_out, nand_7_out, nand_8_out, nand_9_out, nand_10_out, nand_11_out, nand_12_out, nand_13_out,
       nand_14_out, nand_15_out, nand_16_out;

  nand nand_1 (nand_1_out, in_10, in_11);
  not nand_2 (nand_2_out, nand_1_out);  // NAND_Gate
  D_Flip_Flop d_ff_1 (.clk(in_1), .D(in_5), .Q(d_ff_1_q));  // open: Qn, preset, en, reset
  D_Flip_Flop d_ff_2 (.clk(in_2), .D(in_5), .Q(d_ff_2_q));  // open: Qn, preset, en, reset
  D_Flip_Flop d_ff_3 (.clk(in_3), .D(in_5), .Q(d_ff_3_q));  // open: Qn, preset, en, reset
  D_Flip_Flop d_ff_4 (.clk(in_4), .D(in_5), .Q(d_ff_4_q));  // open: Qn, preset, en, reset
  nand nand_3 (nand_3_out, in_7, in_11);
  nand nand_4 (nand_4_out, nand_3_out, in_11);
  nand nand_5 (nand_5_out, in_8, in_11);
  nand nand_6 (nand_6_out, nand_5_out, in_11);
  nand nand_7 (nand_7_out, in_9, in_11);
  nand nand_8 (nand_8_out, nand_7_out, in_11);
  nand nand_9 (nand_9_out, nand_1_out, nand_10_out);
  nand nand_10 (nand_10_out, nand_9_out, nand_2_out);
  and and_1 (out_13, d_ff_1_q, in_6);
  and and_2 (out_14, d_ff_2_q, in_6);
  and and_3 (out_15, d_ff_3_q, in_6);
  and and_4 (out_16, d_ff_4_q, in_6);
  nand nand_11 (nand_11_out, nand_3_out, nand_12_out);
  nand nand_12 (nand_12_out, nand_11_out, nand_4_out);
  nand nand_13 (nand_13_out, nand_5_out, nand_14_out);
  nand nand_14 (nand_14_out, nand_13_out, nand_6_out);
  nand nand_15 (nand_15_out, nand_7_out, nand_16_out);
  nand nand_16 (nand_16_out, nand_15_out, nand_8_out);
  and and_5 (out_20, nand_9_out, in_12);
  and and_6 (out_17, nand_11_out, in_12);
  and and_7 (out_18, nand_13_out, in_12);
  and and_8 (out_19, nand_15_out, in_12);
endmodule
